// Logisim project biblioteca.circ as structural Verilog
module contador8bits (
  input  CLR,
  input  CLK,
  input  [3:0] JMP_Operando,
  input  E,
  input  JMP,
  output Q0,
  output Q1,
  output Q2,
  output Q3,
  output Q4,
  output Q5,
  output Q6,
  output Q7
);

  wire _0, _1, _2, _3, and_1_out, and_2_out, and_3_out, and_4_out, and_5_out, and_6_out, and_7_out,
       and_8_out, and_9_out, and_10_out, and_11_out, and_12_out, and_13_out, and_14_out, JMP_t, not_1_out,
       not_2_out, not_3_out, not_4_out, not_5_out, not_6_out, not_7_out, not_8_out, or_1_out, or_2_out,
       or_3_out, or_4_out, or_5_out, or_6_out, or_7_out, or_8_out;

  D_Flip_Flop d_ff_1 (.clk(CLK), .D(JMP), .Q(JMP_t), .reset(CLR));  // open: Qn, preset
  registrador4bits registrador4bits_1 (.Eclock(CLK), .D(JMP_Operando), .Q({_3, _2, _1, _0}), .CLR(CLR));
  or or_1 (or_1_out, ~JMP_t, _0);  // OR_Gate
  and and_1 (and_1_out, or_1_out, CLR);
  not not_1 (not_1_out, CLK);
  and and_2 (and_2_out, JMP_t, _0);
  T_Flip_Flop #(.Pre_Clr_Positions("BELOW_ABOVE")) t_ff_1 (
    .clk(not_1_out), .T(E), .Q(Q0), .preset(and_2_out), .reset(and_1_out));  // open: Qn
  or or_2 (or_2_out, ~JMP_t, _1);  // OR_Gate
  and and_3 (and_3_out, or_2_out, CLR);
  not not_2 (not_2_out, CLK);
  T_Flip_Flop #(.Pre_Clr_Positions("BELOW_ABOVE")) t_ff_2 (
    .clk(not_2_out), .T(Q0), .Q(Q1), .preset(and_4_out), .reset(and_3_out));  // open: Qn
  and and_4 (and_4_out, JMP_t, _1);
  not not_3 (not_3_out, CLK);
  and and_5 (and_5_out, Q0, Q1);
  or or_3 (or_3_out, ~JMP_t, _2);  // OR_Gate
  and and_6 (and_6_out, or_3_out, CLR);
  T_Flip_Flop #(.Pre_Clr_Positions("BELOW_ABOVE")) t_ff_3 (
    .clk(not_3_out), .T(and_5_out), .Q(Q2), .preset(and_7_out), .reset(and_6_out));  // open: Qn
  and and_7 (and_7_out, JMP_t, _2);
  not not_4 (not_4_out, CLK);
  and and_8 (and_8_out, and_5_out, Q2);
  or or_4 (or_4_out, ~JMP_t, _3);  // OR_Gate
  and and_9 (and_9_out, or_4_out, CLR);
  T_Flip_Flop #(.Pre_Clr_Positions("BELOW_ABOVE")) t_ff_4 (
    .clk(not_4_out), .T(and_8_out), .Q(Q3), .preset(and_10_out), .reset(and_9_out));  // open: Qn
  and and_10 (and_10_out, JMP_t, _3);
  not not_5 (not_5_out, CLK);
  and and_11 (and_11_out, and_8_out, Q3);
  or or_5 (or_5_out, JMP_t, CLR);
  T_Flip_Flop #(.Pre_Clr_Positions("BELOW_ABOVE")) t_ff_5 (
    .clk(not_5_out), .T(and_11_out), .Q(Q4), .preset(1'b0), .reset(or_5_out));  // open: Qn
  or or_6 (or_6_out, JMP_t, CLR);
  not not_6 (not_6_out, CLK);
  and and_12 (and_12_out, and_11_out, Q4);
  T_Flip_Flop #(.Pre_Clr_Positions("BELOW_ABOVE")) t_ff_6 (
    .clk(not_6_out), .T(and_12_out), .Q(Q5), .preset(1'b0), .reset(or_6_out));  // open: Qn
  or or_7 (or_7_out, JMP_t, CLR);
  not not_7 (not_7_out, CLK);
  and and_13 (and_13_out, and_12_out, Q5);
  T_Flip_Flop #(.Pre_Clr_Positions("BELOW_ABOVE")) t_ff_7 (
    .clk(not_7_out), .T(and_13_out), .Q(Q6), .preset(1'b0), .reset(or_7_out));  // open: Qn
  and and_14 (and_14_out, and_13_out, Q6);
  or or_8 (or_8_out, JMP_t, CLR);
  not not_8 (not_8_out, CLK);
  T_Flip_Flop #(.Pre_Clr_Positions("BELOW_ABOVE")) t_ff_8 (
    .clk(not_8_out), .T(and_14_out), .Q(Q7), .preset(1'b0), .reset(or_8_out));  // open: Qn

  // Other names for the same wires on the sheet: JMP_End[3:0] = {_3, _2, _1, _0}
endmodule

module registrador4bits (
  input  CLR,
  input  Eclock,
  input  [3:0] D,
  output [3:0] Q
);

  D_Flip_Flop d_ff_1 (.clk(Eclock), .D(D[3]), .Q(Q[3]), .reset(CLR));  // open: Qn, preset
  D_Flip_Flop d_ff_2 (.clk(Eclock), .D(D[1]), .Q(Q[2]), .reset(CLR));  // open: Qn, preset
  D_Flip_Flop d_ff_3 (.clk(Eclock), .D(D[2]), .Q(Q[1]), .reset(CLR));  // open: Qn, preset
  D_Flip_Flop d_ff_4 (.clk(Eclock), .D(D[0]), .Q(Q[0]), .reset(CLR));  // open: Qn, preset

  // Other names for the same wires on the sheet: CLK = Eclock
endmodule

module unidade_controle (
  input  [1:0] JMP,
  output \Operaçao_de_ULA ,
  output Reinicia_Registradores,
  output Reinicia_Contador,
  output JMP_Para_Operando
);

  Demultiplexer #(.select(2), .enable("false")) demultiplexer_1 (
    .out0(\Operaçao_de_ULA ), .out1(Reinicia_Registradores), .out2(Reinicia_Contador),
    .out3(JMP_Para_Operando), .in(1'b1), .sel(JMP));
endmodule

module RomCpu (
  input  [7:0] busAddr8,
  input  CLK,
  output [15:0] busData16
);

  wire [15:0] ROM_CPU_data;

  Register #(.width(16), .trigger("falling"), .Select("high")) Reg16 (
    .D(ROM_CPU_data), .Q(busData16), .clk(CLK));  // open: en, clr
  ROM #(.dataWidth(16), .Select("low")) ROM_CPU (.addr(busAddr8), .data(ROM_CPU_data));

  // Notes on the sheet:
  //   contents of ROM_CPU (hex, n*v repeats v):
  //   6005 9101 6202 6304 c08 0 0 0 400 6001 9001 9002 6302 6102 9302 6200 6001 800
endmodule
